# Fritzing sketch tactA_breadboard_single (saved by Fritzing 0.9.0b)
breadboards: 1

parts:
  R1 = Resistor [tolerance=±5% resistance=220 package=THT]
  L1 = Inductor [inductance=10mH package="400 mil [THT]"]
  D1 = Rectifier Diode [part_number=1N4001 package="300 mil [THT]"]
  R3 = Resistor [tolerance=±5% resistance=1M package=THT]
  C2 = Ceramic Capacitor [capacitance=100pF package="100 mil [THT, multilayer]"]
  C1 = Ceramic Capacitor [capacitance=10nF voltage=50V package="200 mil [THT, multilayer]"]
  Arduino = Arduino Leonardo (Rev3b)
  R2 = Resistor [tolerance=±5% resistance=3.3k package=THT]

nets:
  N1: R1.Pin_0, Arduino.D9_PWM/A9
  N2: R1.Pin_1, L1.pin_0, R2.Pin_1
  N3: L1.pin_1, D1.anode, C1.0
  N4: D1.cathode, R3.Pin_0, C2.0, Arduino.A0
  N5: R3.Pin_1, C2.1, Arduino.GND, R2.Pin_0

notes:
  Tact Single Sensor Example
  --------------------------------------
  For more information, check https://github.com/StudioNAND/tact-hardware
  Processing lib https://github.com/StudioNAND/tact-processing
  Arduino sketch https://github.com/StudioNAND/tact-arduino-sketch
  Arduino library https://github.com/philippschmitt/tact-arduino
  This circuit is inspired by Mads Hobye's instructables tutorial
  http://www.instructables.com/id/Touche-for-Arduino-Advanced-touch-sensing/
  Cheers!
  Sensor
